// Logisim project drisc.circ as structural Verilog: 15 circuits, main circuit main
module main (
  input  in_1,
  input  in_2,
  input  in_3,
  input  in_4,
  input  in_5,
  input  in_6,
  input  in_7,
  input  [2:0] in_8
);

  wire alu_1_p2, Alu_Enable, and_1_out, clock_1_out, clock_circuit_1_phase1n, clock_circuit_1_phase1s,
       clock_circuit_1_phase2i, clock_circuit_1_phase2n, clock_circuit_1_phase2s, clock_circuit_1_phase3,
       clock_circuit_1_phase3i, clock_circuit_1_phase3s, Load, Load_Immediate_High,
       operation_controller_1_get_last_program_counter, operation_controller_1_interrupt,
       operation_controller_1_jump, por_1_out, por_2_out, por_3_out, por_4_out, por_5_out, por_6_out, Shift,
       shift_register_1_p5, shift_register_1_p8, shift_register_1_p9, Signed_Load, Store;
  wire [0:0] immediate_register_1_immediate_flag;
  wire [1:0] DataSize, Shift_Operation;
  wire [2:0] clock_circuit_1_phase3n;
  wire [3:0] alu_1_p15, Alu_Operation;
  wire [4:0] immediate_register_1_shift_amount;
  wire [31:0] alu_1_p4, alu_1_p19, buffer_1_out, buffer_2_out, data_input_output_1_lbus_out,
       data_input_output_1_pbus_out, immediate_register_1_high_immediate_19bit,
       immediate_register_1_immediate_13bit, program_counter_1_c_bus_out, program_counter_1_p_bus_out,
       register_file_1_a_bus_out, register_file_1_b_bus_out, shifter_circuit_1_c_bus_out;

  POR #(.PorHighDuration(1), .porsize(2)) por_1 (.out(por_1_out));
  POR #(.porsize(2)) por_2 (.out(por_2_out));
  Clock clock_1 (.out(clock_1_out));
  // Shift_Register #(.length(3)) shift_register_1: pin names not known; wires that end beside it: por_1_out, por_2_out, 1'b1, clock_1_out, shift_register_1_p5, 1'b1, 1'b0, shift_register_1_p8, shift_register_1_p9, shift_register_1_p5
  POR #(.PorHighDuration(3), .porsize(2)) por_3 (.out(por_3_out));
  Clock_Circuit clock_circuit_1 (
    .Phase3_in(shift_register_1_p5), .Load_Store_Instruction(in_3), .Window_Overflow(in_1),
    .Return_Interrupt_Instruction(in_2), .Interrupt(operation_controller_1_interrupt), .Reset(por_3_out),
    .Phase1_In(shift_register_1_p8), .Phase2_In(shift_register_1_p9), .Phase3(clock_circuit_1_phase3),
    .Phase3i(clock_circuit_1_phase3i), .Phase3n(clock_circuit_1_phase3n[0]),
    .Phase3s(clock_circuit_1_phase3s), .Phase1(clock_circuit_1_phase3n[2]),
    .Phase1n(clock_circuit_1_phase1n), .Phase1s(clock_circuit_1_phase1s),
    .Phase2(clock_circuit_1_phase3n[1]), .Phase2i(clock_circuit_1_phase2i),
    .Phase2n(clock_circuit_1_phase2n), .Phase2s(clock_circuit_1_phase2s));
  POR #(.PorHighDuration(1), .porsize(2)) por_4 (.out(por_4_out));
  Register_File register_file_1 (
    .C_Bus_In(buffer_2_out), .P_Bus_in(buffer_1_out), .Reset(por_4_out), .Phase2(clock_circuit_1_phase3n[1]),
    .Phase2s(clock_circuit_1_phase2s), .Phase2n(clock_circuit_1_phase2n), .Phase1n(clock_circuit_1_phase1n),
    .Phase3n(clock_circuit_1_phase3n[0]), .Window_Number(in_8), .A_Bus_Out(register_file_1_a_bus_out),
    .B_Bus_Out(register_file_1_b_bus_out));
  // Probe on buffer_1_out
  // Probe on register_file_1_a_bus_out
  // Probe on register_file_1_b_bus_out
  // Probe on buffer_2_out
  assign buffer_1_out = data_input_output_1_pbus_out;  // Buffer buffer_1, 32 bits wide
  Data_Input_Output data_input_output_1 (
    .Data_Size(DataSize), .Load(Load), .Store(Store), .LBus_In(data_input_output_1_lbus_out),
    .PBus_In(data_input_output_1_pbus_out), .Phase1s(clock_circuit_1_phase1s),
    .Phase2s(clock_circuit_1_phase2s), .Signed_Data(Signed_Load), .Lbus_Out(data_input_output_1_lbus_out),
    .PBus_Out(data_input_output_1_pbus_out));
  Shifter_Circuit shifter_circuit_1 (
    .Phi3n(clock_circuit_1_phase3n[0]), .Select_Immediate(immediate_register_1_immediate_flag[0]),
    .B_Bus_In(register_file_1_a_bus_out), .Immediate_In(immediate_register_1_shift_amount),
    .Byte_Control_In(DataSize), .Load(Load), .Store(Store), .Shift(Shift),
    .LBus_In(data_input_output_1_lbus_out), .Phi1(clock_circuit_1_phase3n[2]),
    .Operation_Select(Shift_Operation), .Phi2(clock_circuit_1_phase3n[1]),
    .C_Bus_Out(shifter_circuit_1_c_bus_out), .LBus_Out(data_input_output_1_lbus_out));  // open: A_Bus_In
  assign buffer_2_out = shifter_circuit_1_c_bus_out;  // Buffer buffer_2, 32 bits wide
  POR #(.PorHighDuration(4), .porsize(2)) por_5 (.out(por_5_out));
  // Probe on shifter_circuit_1_c_bus_out
  Immediate_Register immediate_register_1 (
    .Pbus_In(buffer_1_out), .Write_Enable(por_5_out), .Immediate_13bit(immediate_register_1_immediate_13bit),
    .High_Immediate_19bit(immediate_register_1_high_immediate_19bit),
    .Shift_Amount(immediate_register_1_shift_amount), .Immediate_Flag(immediate_register_1_immediate_flag[0]));
  // ALU alu_1: pin names not known; wires that end beside it: in_4, alu_1_p2, register_file_1_a_bus_out, alu_1_p4, {Load_Immediate_High, immediate_register_1_immediate_flag[0]}, register_file_1_b_bus_out, immediate_register_1_immediate_13bit, immediate_register_1_high_immediate_19bit, Alu_Operation, Alu_Enable, clock_circuit_1_phase3n[2], clock_circuit_1_phase3n[1], clock_circuit_1_phase3, clock_circuit_1_phase3s, alu_1_p15[0], alu_1_p15[1], alu_1_p15[2], alu_1_p15[3], alu_1_p19
  // Probe on alu_1_p19
  assign buffer_2_out = alu_1_p19;  // Buffer buffer_3, 32 bits wide
  Operation_Controller operation_controller_1 (
    .P_Bus_In(buffer_1_out), .Phase2n(clock_circuit_1_phase2n), .CNZV_In(alu_1_p15),
    .Phase1(clock_circuit_1_phase3n[2]), .Data_Size(DataSize), .Shift_Operation(Shift_Operation),
    .Shift(Shift), .Load_Immediate_High(Load_Immediate_High), .ALU_Enabled(Alu_Enable),
    .ALU_Operation(Alu_Operation),
    .Get_Last_Program_Counter(operation_controller_1_get_last_program_counter),
    .Interrupt(operation_controller_1_interrupt), .Load(Load), .Store(Store), .Signed_Load(Signed_Load),
    .Jump(operation_controller_1_jump));  // open: Call, Return_Instruction, Relative, No_Destination, Jump_Instruction
  POR #(.PorHighDuration(3), .porsize(2)) por_6 (.out(por_6_out));
  Program_Counter program_counter_1 (
    .Enable_Current_Out(in_5), .Phase1n(clock_circuit_1_phase1n),
    .Enable_Last_Out(operation_controller_1_get_last_program_counter), .Reset(por_6_out),
    .Phase_3n(clock_circuit_1_phase3n[0]), .Phase_3i(clock_circuit_1_phase3i),
    .Phase2(clock_circuit_1_phase3n[1]), .Enable_Output_Out(in_6), .D_Bus_In(alu_1_p19),
    .Jump(operation_controller_1_jump), .Enable_Bridge_Out(in_7), .Phase2n(clock_circuit_1_phase2n),
    .Program_Counter_Out(alu_1_p4), .C_Bus_Out(program_counter_1_c_bus_out),
    .P_Bus_Out(program_counter_1_p_bus_out));
  assign buffer_1_out = program_counter_1_p_bus_out;  // Buffer buffer_4, 32 bits wide
  // Probe on program_counter_1_c_bus_out
  assign buffer_2_out = program_counter_1_c_bus_out;  // Buffer buffer_5, 32 bits wide
  // Probe on register_file_1_a_bus_out
  // Probe on register_file_1_b_bus_out
  // Probe on buffer_2_out
  and and_1 (and_1_out, Store, clock_circuit_1_phase2n);
  POR #(.PorHighDuration(1), .porsize(2)) por_7 ();  // open: out
  RAM #(.addrWidth(24), .clearpin("true"), .dataWidth(32), .databus("bidir"), .trigger("high")) ram_1 (
    .addr(alu_1_p4[23:0]), .we(and_1_out), .oe(clock_circuit_1_phase2n), .data(buffer_1_out));  // open: clr

  // Notes on the sheet:
  //   P Bus
  //   A bus
  //   B bus
  //   C bus
  //   Program Counter(Dline)
endmodule

module Clock_Circuit (
  input  Interrupt,
  input  Reset,
  input  Phase1_In,
  input  Phase2_In,
  input  Phase3_in,
  input  Load_Store_Instruction,
  input  Window_Overflow,
  input  Return_Interrupt_Instruction,
  output Phase2n,
  output Phase1,
  output Phase1s,
  output Phase2,
  output Phase3,
  output Phase3n,
  output Phase2s,
  output Phase1n,
  output Phase2i,
  output Phase3i,
  output Phase3s
);

  wire and_1_out, and_2_out, and_8_out, and_12_out, Interrupt_Enable_q, Interruption_q, not_1_out, not_2_out,
       not_3_out, or_1_out, or_2_out, SecondaryA_q, SecondaryB_q;

  and and_1 (and_1_out, Return_Interrupt_Instruction, Phase3n);
  or or_1 (or_1_out, Interrupt, Window_Overflow);
  Register #(.trigger("high"), .width(1)) Interrupt_Enable (
    .D(and_1_out), .en(and_1_out), .clk(1'b1), .Q(Interrupt_Enable_q), .clr(Phase2i));
  and and_2 (and_2_out, or_1_out, Interrupt_Enable_q);
  or or_2 (or_2_out, Reset, and_2_out);
  and and_3 (Phase1n, not_2_out, Phase1_In);
  and and_4 (Phase1s, SecondaryA_q, Phase1_In);
  Register #(.trigger("high"), .width(1)) Interruption (
    .D(or_2_out), .en(Phase1_In), .clk(Phase1_In), .Q(Interruption_q));  // open: clr
  not not_1 (not_1_out, Interruption_q);
  and and_5 (Phase2i, Interruption_q, Phase2_In);
  and and_6 (Phase2n, not_3_out, not_1_out, Phase2_In);
  and and_7 (Phase2s, SecondaryB_q, not_1_out, Phase2_In);
  Register #(.trigger("high"), .width(1)) SecondaryA (
    .D(and_8_out), .en(Phase2_In), .clk(Phase2_In), .Q(SecondaryA_q));  // open: clr
  and and_8 (and_8_out, Load_Store_Instruction, not_3_out);
  not not_2 (not_2_out, SecondaryA_q);
  and and_9 (Phase3i, Interruption_q, Phase3_in);
  and and_10 (Phase3n, not_2_out, not_1_out, Phase3_in);
  and and_11 (Phase3s, SecondaryA_q, not_1_out, Phase3_in);
  Register #(.trigger("high"), .width(1)) SecondaryB (
    .D(and_12_out), .en(Phase3_in), .clk(Phase3_in), .Q(SecondaryB_q));  // open: clr
  and and_12 (and_12_out, not_1_out, SecondaryA_q);
  not not_3 (not_3_out, SecondaryB_q);

  assign Phase1 = Phase1_In;
  assign Phase2 = Phase2_In;
  assign Phase3 = Phase3_in;
endmodule

module ALU (
  input  [3:0] Operation,
  input  Phase1,
  input  Phase3,
  input  Enable_Output,
  input  Carry_In,
  input  Phase2,
  input  [1:0] Input_Select1,
  input  [31:0] Source1,
  input  [31:0] Program_Counter_In,
  input  [1:0] Input_Select2,
  input  [31:0] Source2,
  input  [31:0] Immediate_13bit,
  input  [31:0] High_Immediate_19bit,
  output [31:0] Result,
  output [31:0] Result_Negated,
  output Zero,
  output Negative,
  output Overflow,
  output Carry_Out
);

  wire adder_1_cout, and_1_out, and_3_out, subtractor_1_bout;
  wire [30:0] register_3_q;
  wire [31:0] adder_1_out, and_2_out, multiplexer_1_out, multiplexer_2_out, multiplexer_3_out,
       multiplexer_4_out, multiplexer_6_out, not_1_out, or_1_out, register_1_q, register_2_q,
       subtractor_1_out, xor_1_out;

  Multiplexer #(.select(2), .width(32)) multiplexer_1 (
    .in0(Source1), .in1(Source1), .in2(Program_Counter_In), .in3({32{1'b0}}), .out(multiplexer_1_out),
    .sel(Input_Select1));
  Multiplexer #(.select(2), .width(32)) multiplexer_2 (
    .in0(Source2), .in1(Immediate_13bit), .in2(Immediate_13bit), .in3(High_Immediate_19bit),
    .out(multiplexer_2_out), .sel(Input_Select2));
  Register #(.trigger("high"), .width(32)) register_1 (
    .D(multiplexer_1_out), .en(Phase1), .clk(Phase1), .Q(register_1_q));  // open: clr
  Register #(.trigger("high"), .width(32)) register_2 (
    .D(multiplexer_2_out), .en(Phase1), .clk(Phase1), .Q(register_2_q));  // open: clr
  // Probe on register_1_q
  // Probe on register_2_q
  Multiplexer #(.width(32)) multiplexer_3 (
    .in0(register_1_q), .in1(register_2_q), .out(multiplexer_3_out), .sel(Operation[3]));
  Multiplexer #(.width(32)) multiplexer_4 (
    .in0(register_2_q), .in1(register_1_q), .out(multiplexer_4_out), .sel(Operation[3]));
  and and_1 (and_1_out, Carry_In, Operation[0]);
  assign and_2_out = multiplexer_3_out & multiplexer_4_out;  // AND_Gate and_2, 32 bits wide
  assign xor_1_out = multiplexer_3_out ^ multiplexer_4_out;  // XOR_Gate xor_1, 32 bits wide
  assign or_1_out = multiplexer_3_out | multiplexer_4_out;  // OR_Gate or_1, 32 bits wide
  Subtractor #(.width(32)) subtractor_1 (
    .a(multiplexer_3_out), .b(multiplexer_4_out), .out(subtractor_1_out), .bin(and_1_out),
    .bout(subtractor_1_bout));
  Adder #(.width(32)) adder_1 (
    .a(multiplexer_3_out), .b(multiplexer_4_out), .out(adder_1_out), .cin(and_1_out), .cout(adder_1_cout));
  Multiplexer multiplexer_5 (.in0(subtractor_1_bout), .in1(adder_1_cout), .out(Carry_Out), .sel(Operation[1]));
  Multiplexer #(.select(3), .width(32)) multiplexer_6 (
    .in0(multiplexer_4_out), .in1(and_2_out), .in2(xor_1_out), .in3(or_1_out), .in4(subtractor_1_out),
    .in5(subtractor_1_out), .in6(adder_1_out), .in7(adder_1_out), .out(multiplexer_6_out),
    .sel(Operation[2:0]));
  Register #(.trigger("high"), .width(32)) register_3 (
    .D(multiplexer_6_out), .en(Phase2), .clk(Phase2), .Q({Negative, register_3_q}));  // open: clr
  assign not_1_out = ~{Negative, register_3_q};  // NOT_Gate not_1, 32 bits wide
  nor nor_1 (Zero, register_3_q[0], register_3_q[1], register_3_q[2], register_3_q[3], register_3_q[4], register_3_q[5], register_3_q[6], register_3_q[7], register_3_q[8], register_3_q[9], register_3_q[10], register_3_q[11], register_3_q[12], register_3_q[13], register_3_q[14], register_3_q[15], register_3_q[16], register_3_q[17], register_3_q[18], register_3_q[19], register_3_q[20], register_3_q[21], register_3_q[22], register_3_q[23], register_3_q[24], register_3_q[25], register_3_q[26], register_3_q[27], register_3_q[28], register_3_q[29], register_3_q[30], Negative);
  xor xor_2 (Overflow, Negative, Carry_Out);
  assign Result_Negated = and_3_out ? not_1_out : 32'bz;  // Controlled_Buffer controlled_buffer_1
  and and_3 (and_3_out, Phase3, Enable_Output);
  assign Result = and_3_out ? {Negative, register_3_q} : 32'bz;  // Controlled_Buffer controlled_buffer_2

  // Notes on the sheet:
  //   Source1: initial=0xffffffff
endmodule

module Program_Counter (
  input  Phase2n,
  input  Phase1n,
  input  Phase2,
  input  Reset,
  input  Enable_Current_Out,
  input  Enable_Last_Out,
  input  Enable_Output_Out,
  input  [31:0] D_Bus_In,
  input  Jump,
  input  Enable_Bridge_Out,
  input  Phase_3n,
  input  Phase_3i,
  output [31:0] Program_Counter_Out,
  output [31:0] C_Bus_Out,
  output [31:0] P_Bus_Out
);

  wire and_1_out, or_1_out;
  wire [29:0] adder_1_out, controlled_buffer_1_out, Last_q, Output_Latch_q, register_1_q;

  or or_1 (or_1_out, Phase_3n, Phase_3i);
  Register #(.trigger("high"), .width(30)) Output_Latch (
    .D(adder_1_out), .en(Phase2), .clk(Phase2), .Q(Output_Latch_q), .clr(Reset));
  Adder #(.width(30)) adder_1 (.a(register_1_q), .b(30'h1), .out(adder_1_out));  // open: cin, cout
  assign controlled_buffer_1_out = Jump ? D_Bus_In[31:2] : 30'bz;  // Controlled_Buffer controlled_buffer_1
  assign controlled_buffer_1_out = and_1_out ? Output_Latch_q : 30'bz;  // Controlled_Buffer controlled_buffer_2
  and and_1 (and_1_out, ~Jump, Phase_3n);  // AND_Gate
  Register #(.trigger("high"), .width(30)) register_1 (
    .D(controlled_buffer_1_out), .en(or_1_out), .clk(or_1_out), .Q(register_1_q), .clr(Reset));
  assign P_Bus_Out[31:2] = Enable_Output_Out ? Output_Latch_q : 30'bz;  // Controlled_Buffer controlled_buffer_3
  assign P_Bus_Out[31:2] = Enable_Bridge_Out ? controlled_buffer_1_out : 30'bz;  // Controlled_Buffer controlled_buffer_4
  Register #(.width(30)) Current (
    .D(register_1_q), .en(1'b1), .clk(Phase2n), .Q(Program_Counter_Out[31:2]), .clr(Reset));
  assign P_Bus_Out[31:2] = Phase_3i ? {30{1'b0}} : 30'bz;  // Controlled_Buffer Interrupt_Vector
  assign C_Bus_Out = Enable_Current_Out ? {Program_Counter_Out[31:2], 2'b00} : 32'bz;  // Controlled_Buffer controlled_buffer_5
  Register #(.trigger("high"), .width(30)) Last (
    .D(Program_Counter_Out[31:2]), .en(1'b1), .clk(Phase1n), .Q(Last_q), .clr(Reset));
  assign C_Bus_Out = Enable_Last_Out ? {Last_q, 2'b00} : 32'bz;  // Controlled_Buffer controlled_buffer_6

  assign Program_Counter_Out[1:0] = 2'b00;

  // Notes on the sheet:
  //   Next
endmodule

module Immediate_Register (
  input  [31:0] Pbus_In,
  input  Write_Enable,
  output [4:0] Shift_Amount,
  output [31:0] Immediate_13bit,
  output Immediate_Flag,
  output [31:0] High_Immediate_19bit
);

  Register #(.trigger("high"), .width(19)) register_1 (
    .D(Pbus_In[18:0]), .en(Write_Enable), .clk(1'b1), .Q(High_Immediate_19bit[31:13]));  // open: clr
  assign Immediate_13bit = {{19{High_Immediate_19bit[25]}}, High_Immediate_19bit[25:13]};  // Bit_Extender bit_extender_1

  assign High_Immediate_19bit[12:0] = {13{1'b0}};
  assign Immediate_Flag = High_Immediate_19bit[26];
  assign Shift_Amount = High_Immediate_19bit[17:13];
endmodule

module Data_Input_Output (
  input  Phase1s,
  input  Phase2s,
  input  Signed_Data,
  input  [1:0] Data_Size,
  input  Load,
  input  Store,
  input  [31:0] PBus_In,
  input  [31:0] LBus_In,
  output [31:0] PBus_Out,
  output [31:0] Lbus_Out
);

  wire and_1_out, and_2_out, and_3_out, and_4_out, and_5_out, or_1_out;
  wire [7:0] bit_extender_1_out, bit_extender_2_out, bit_extender_3_out, multiplexer_1_out,
       multiplexer_2_out, multiplexer_3_out, multiplexer_4_out, multiplexer_5_out, multiplexer_6_out,
       multiplexer_7_out, register_1_q, register_2_q, register_3_q, register_4_q;
  wire [31:0] controlled_buffer_2_out, controlled_buffer_7_out;

  assign PBus_Out = Phase2s ? controlled_buffer_2_out : 32'bz;  // Controlled_Buffer controlled_buffer_1
  assign controlled_buffer_2_out = Phase1s ? PBus_In : 32'bz;  // Controlled_Buffer controlled_buffer_2
  assign controlled_buffer_2_out[7:0] = Phase2s ? register_1_q : 8'bz;  // Controlled_Buffer controlled_buffer_3
  assign controlled_buffer_2_out[15:8] = Phase2s ? register_2_q : 8'bz;  // Controlled_Buffer controlled_buffer_4
  assign controlled_buffer_2_out[23:16] = Phase2s ? register_3_q : 8'bz;  // Controlled_Buffer controlled_buffer_5
  assign controlled_buffer_2_out[31:24] = Phase2s ? register_4_q : 8'bz;  // Controlled_Buffer controlled_buffer_6
  Multiplexer #(.width(8)) multiplexer_1 (
    .in0(controlled_buffer_2_out[7:0]), .in1(controlled_buffer_7_out[7:0]), .out(multiplexer_1_out),
    .sel(and_5_out));
  Multiplexer #(.width(8)) multiplexer_2 (
    .in0(controlled_buffer_2_out[15:8]), .in1(controlled_buffer_7_out[15:8]), .out(multiplexer_2_out),
    .sel(and_5_out));
  Multiplexer #(.width(8)) multiplexer_3 (
    .in0(controlled_buffer_2_out[23:16]), .in1(controlled_buffer_7_out[23:16]), .out(multiplexer_3_out),
    .sel(and_5_out));
  Multiplexer #(.width(8)) multiplexer_4 (
    .in0(controlled_buffer_2_out[31:24]), .in1(controlled_buffer_7_out[31:24]), .out(multiplexer_4_out),
    .sel(and_5_out));
  or or_1 (or_1_out, Phase1s, and_5_out);
  Register #(.trigger("high")) register_1 (
    .D(multiplexer_1_out), .en(or_1_out), .clk(or_1_out), .Q(register_1_q));  // open: clr
  Register #(.trigger("high")) register_2 (
    .D(multiplexer_2_out), .en(or_1_out), .clk(or_1_out), .Q(register_2_q));  // open: clr
  Register #(.trigger("high")) register_3 (
    .D(multiplexer_3_out), .en(or_1_out), .clk(or_1_out), .Q(register_3_q));  // open: clr
  Register #(.trigger("high")) register_4 (
    .D(multiplexer_4_out), .en(or_1_out), .clk(or_1_out), .Q(register_4_q));  // open: clr
  and and_1 (and_1_out, Signed_Data, register_1_q[7]);
  and and_2 (and_2_out, Signed_Data, multiplexer_5_out[7]);
  and and_3 (and_3_out, Signed_Data, multiplexer_6_out[7]);
  assign bit_extender_1_out = {{7{and_1_out}}, and_1_out};  // Bit_Extender bit_extender_1
  Multiplexer #(.width(8)) multiplexer_5 (
    .in0(bit_extender_1_out), .in1(register_2_q), .out(multiplexer_5_out), .sel(Data_Size[0]));
  assign bit_extender_2_out = {{7{and_2_out}}, and_2_out};  // Bit_Extender bit_extender_2
  Multiplexer #(.width(8)) multiplexer_6 (
    .in0(bit_extender_2_out), .in1(register_3_q), .out(multiplexer_6_out), .sel(Data_Size[1]));
  assign bit_extender_3_out = {{7{and_3_out}}, and_3_out};  // Bit_Extender bit_extender_3
  Multiplexer #(.width(8)) multiplexer_7 (
    .in0(bit_extender_3_out), .in1(register_4_q), .out(multiplexer_7_out), .sel(Data_Size[1]));
  assign controlled_buffer_7_out[7:0] = and_4_out ? register_1_q : 8'bz;  // Controlled_Buffer controlled_buffer_7
  assign controlled_buffer_7_out[15:8] = and_4_out ? multiplexer_5_out : 8'bz;  // Controlled_Buffer controlled_buffer_8
  assign controlled_buffer_7_out[23:16] = and_4_out ? multiplexer_6_out : 8'bz;  // Controlled_Buffer controlled_buffer_9
  assign controlled_buffer_7_out[31:24] = and_4_out ? multiplexer_7_out : 8'bz;  // Controlled_Buffer controlled_buffer_10
  and and_4 (and_4_out, Phase2s, Load);
  and and_5 (and_5_out, Phase2s, Store);
  assign Lbus_Out = and_4_out ? controlled_buffer_7_out : 32'bz;  // Controlled_Buffer controlled_buffer_11
  assign controlled_buffer_7_out = and_5_out ? LBus_In : 32'bz;  // Controlled_Buffer controlled_buffer_12

  // Notes on the sheet:
  //   LBus_In: initial=0xe3e3e3e3
  //   PBus_In: initial=0xf2f2f2f2
endmodule

module Shifter_Circuit (
  input  Load,
  input  Store,
  input  Shift,
  input  Phi3n,
  input  Select_Immediate,
  input  [31:0] B_Bus_In,
  input  [4:0] Immediate_In,
  input  [1:0] Byte_Control_In,
  input  [1:0] Operation_Select,
  input  Phi1,
  input  [31:0] A_Bus_In,
  input  Phi2,
  input  [31:0] LBus_In,
  output [31:0] C_Bus_Out,
  output [31:0] LBus_Out
);

  wire and_1_out, or_1_out, or_2_out, or_3_out;
  wire [4:0] multiplexer_1_out, multiplexer_2_out, Shift_Amount_Latch_q;
  wire [31:0] controlled_buffer_1_out, multiplexer_3_out, Shift_In_Latch_q, Shift_Out_Latch_q, shifter_1_out,
       shifter_2_out, shifter_3_out;

  Multiplexer #(.width(5)) multiplexer_1 (
    .in0(B_Bus_In[4:0]), .in1(Immediate_In), .out(multiplexer_1_out), .sel(Select_Immediate));
  or or_1 (or_1_out, Load, Store);
  Multiplexer #(.width(5)) multiplexer_2 (
    .in0(multiplexer_1_out), .in1({Byte_Control_In, 3'b000}), .out(multiplexer_2_out), .sel(or_1_out));
  assign controlled_buffer_1_out = Load ? LBus_In : 32'bz;  // Controlled_Buffer controlled_buffer_1
  assign LBus_Out = Store ? controlled_buffer_1_out : 32'bz;  // Controlled_Buffer controlled_buffer_2
  Register #(.trigger("high"), .width(5)) Shift_Amount_Latch (
    .D(multiplexer_2_out), .en(Phi1), .clk(Phi1), .Q(Shift_Amount_Latch_q));  // open: clr
  Register #(.trigger("high"), .width(32)) Shift_In_Latch (
    .D(A_Bus_In), .en(Phi1), .clk(Phi1), .Q(Shift_In_Latch_q));  // open: clr
  or or_2 (or_2_out, Shift, Store);
  assign controlled_buffer_1_out = or_2_out ? Shift_In_Latch_q : 32'bz;  // Controlled_Buffer controlled_buffer_3
  Shifter #(.width(32)) shifter_1 (.in(controlled_buffer_1_out), .\dist (Shift_Amount_Latch_q), .out(shifter_1_out));
  Shifter #(.shift("lr"), .width(32)) shifter_2 (
    .in(controlled_buffer_1_out), .\dist (Shift_Amount_Latch_q), .out(shifter_2_out));
  Shifter #(.shift("ar"), .width(32)) shifter_3 (
    .in(controlled_buffer_1_out), .\dist (Shift_Amount_Latch_q), .out(shifter_3_out));
  Multiplexer #(.select(2), .width(32)) multiplexer_3 (
    .in0(shifter_1_out), .in1(shifter_2_out), .in2(shifter_3_out), .in3(shifter_3_out),
    .out(multiplexer_3_out), .sel(Operation_Select));
  Register #(.trigger("high"), .width(32)) Shift_Out_Latch (
    .D(multiplexer_3_out), .en(Phi2), .clk(Phi2), .Q(Shift_Out_Latch_q));  // open: clr
  or or_3 (or_3_out, Shift, Load);
  and and_1 (and_1_out, or_3_out, Phi3n);
  assign C_Bus_Out = and_1_out ? Shift_Out_Latch_q : 32'bz;  // Controlled_Buffer controlled_buffer_4
endmodule

module Register_Window (
  input  [3:0] Address_A,
  input  Read_Enable_A,
  input  Reset,
  input  [31:0] Data_In,
  input  [3:0] Address_C,
  input  Write_Enable,
  input  [3:0] Address_B,
  input  Read_Enable_B,
  output [31:0] A_Data_Out,
  output [31:0] B_Data_Out
);

  wire decoder_1_out0, decoder_1_out1, decoder_1_out2, decoder_1_out3, decoder_1_out4, decoder_1_out5,
       decoder_1_out6, decoder_1_out7, decoder_1_out8, decoder_1_out9, decoder_1_out10, decoder_1_out11,
       decoder_1_out12, decoder_1_out13, decoder_1_out14, decoder_1_out15;
  wire [31:0] Reg0_q, Reg1_q, Reg2_q, Reg3_q, Reg4_q, Reg5_q, Reg6_q, Reg7_q, Reg8_q, Reg9_q, RegA_q, RegB_q,
       RegC_q, RegD_q, RegE_q, RegF_q;

  Decoder #(.select(4)) decoder_1 (
    .out0(decoder_1_out0), .out1(decoder_1_out1), .out2(decoder_1_out2), .out3(decoder_1_out3),
    .out4(decoder_1_out4), .out5(decoder_1_out5), .out6(decoder_1_out6), .out7(decoder_1_out7),
    .out8(decoder_1_out8), .out9(decoder_1_out9), .out10(decoder_1_out10), .out11(decoder_1_out11),
    .out12(decoder_1_out12), .out13(decoder_1_out13), .out14(decoder_1_out14), .out15(decoder_1_out15),
    .sel(Address_C), .en(Write_Enable));
  Register #(.trigger("high"), .width(32)) Reg0 (
    .D(Data_In), .en(decoder_1_out0), .clk(decoder_1_out0), .Q(Reg0_q), .clr(Reset));
  Register #(.trigger("high"), .width(32)) Reg2 (
    .D(Data_In), .en(decoder_1_out2), .clk(decoder_1_out2), .Q(Reg2_q), .clr(Reset));
  Register #(.trigger("high"), .width(32)) Reg4 (
    .D(Data_In), .en(decoder_1_out4), .clk(decoder_1_out4), .Q(Reg4_q), .clr(Reset));
  Register #(.trigger("high"), .width(32)) Reg6 (
    .D(Data_In), .en(decoder_1_out6), .clk(decoder_1_out6), .Q(Reg6_q), .clr(Reset));
  Register #(.trigger("high"), .width(32)) Reg8 (
    .D(Data_In), .en(decoder_1_out8), .clk(decoder_1_out8), .Q(Reg8_q), .clr(Reset));
  Register #(.trigger("high"), .width(32)) RegA (
    .D(Data_In), .en(decoder_1_out10), .clk(decoder_1_out10), .Q(RegA_q), .clr(Reset));
  Register #(.trigger("high"), .width(32)) RegC (
    .D(Data_In), .en(decoder_1_out12), .clk(decoder_1_out12), .Q(RegC_q), .clr(Reset));
  Register #(.trigger("high"), .width(32)) RegE (
    .D(Data_In), .en(decoder_1_out14), .clk(decoder_1_out14), .Q(RegE_q), .clr(Reset));
  Register #(.trigger("high"), .width(32)) Reg1 (
    .D(Data_In), .en(decoder_1_out1), .clk(decoder_1_out1), .Q(Reg1_q), .clr(Reset));
  Register #(.trigger("high"), .width(32)) Reg3 (
    .D(Data_In), .en(decoder_1_out3), .clk(decoder_1_out3), .Q(Reg3_q), .clr(Reset));
  Register #(.trigger("high"), .width(32)) Reg5 (
    .D(Data_In), .en(decoder_1_out5), .clk(decoder_1_out5), .Q(Reg5_q), .clr(Reset));
  Register #(.trigger("high"), .width(32)) Reg7 (
    .D(Data_In), .en(decoder_1_out7), .clk(decoder_1_out7), .Q(Reg7_q), .clr(Reset));
  Register #(.trigger("high"), .width(32)) Reg9 (
    .D(Data_In), .en(decoder_1_out9), .clk(decoder_1_out9), .Q(Reg9_q), .clr(Reset));
  Register #(.trigger("high"), .width(32)) RegB (
    .D(Data_In), .en(decoder_1_out11), .clk(decoder_1_out11), .Q(RegB_q), .clr(Reset));
  Register #(.trigger("high"), .width(32)) RegD (
    .D(Data_In), .en(decoder_1_out13), .clk(decoder_1_out13), .Q(RegD_q), .clr(Reset));
  Register #(.trigger("high"), .width(32)) RegF (
    .D(Data_In), .en(decoder_1_out15), .clk(decoder_1_out15), .Q(RegF_q), .clr(Reset));
  Multiplexer #(.disabled("Z"), .enable("true"), .select(4), .width(32)) multiplexer_1 (
    .in0(Reg0_q), .in1(Reg1_q), .in2(Reg2_q), .in3(Reg3_q), .in4(Reg4_q), .in5(Reg5_q), .in6(Reg6_q),
    .in7(Reg7_q), .in8(Reg8_q), .in9(Reg9_q), .in10(RegA_q), .in11(RegB_q), .in12(RegC_q), .in13(RegD_q),
    .in14(RegE_q), .in15(RegF_q), .out(A_Data_Out), .sel(Address_A), .en(Read_Enable_A));
  Multiplexer #(.disabled("Z"), .enable("true"), .select(4), .width(32)) multiplexer_2 (
    .in0(Reg0_q), .in1(Reg1_q), .in2(Reg2_q), .in3(Reg3_q), .in4(Reg4_q), .in5(Reg5_q), .in6(Reg6_q),
    .in7(Reg7_q), .in8(Reg8_q), .in9(Reg9_q), .in10(RegA_q), .in11(RegB_q), .in12(RegC_q), .in13(RegD_q),
    .in14(RegE_q), .in15(RegF_q), .out(B_Data_Out), .sel(Address_B), .en(Read_Enable_B));
endmodule

module Register_File (
  input  [31:0] P_Bus_in,
  input  Phase2,
  input  Phase2s,
  input  Phase2n,
  input  [31:0] C_Bus_In,
  input  [2:0] Window_Number,
  input  Reset,
  input  Phase1n,
  input  Phase3n,
  output [31:0] A_Bus_Out,
  output [31:0] B_Bus_Out
);

  wire or_1_out;
  wire [2:0] A_Address_q_2, and_1_out, cwp_and_address_decoder_1_decoded_enables,
       cwp_and_address_decoder_1_decoded_enables_2, cwp_and_address_decoder_1_decoded_enables_3,
       cwp_and_address_decoder_1_decoded_enables_4, cwp_and_address_decoder_1_decoded_enables_5,
       cwp_and_address_decoder_1_decoded_enables_6, cwp_and_address_decoder_1_decoded_enables_7,
       cwp_and_address_decoder_1_decoded_enables_8;
  wire [3:0] A_Address_q, B_Address_q, C_Address_q;
  wire [4:0] multiplexer_1_out, register_1_q, register_2_q, register_3_q;

  Register #(.trigger("high"), .width(5)) register_1 (
    .D(P_Bus_in[31:27]), .en(Phase2), .clk(Phase2), .Q(register_1_q), .clr(Reset));
  Register #(.trigger("high"), .width(5)) register_2 (
    .D(P_Bus_in[17:13]), .en(Phase2), .clk(Phase2), .Q(register_2_q), .clr(Reset));
  Register #(.trigger("high"), .width(5)) register_3 (
    .D(P_Bus_in[12:8]), .en(Phase2), .clk(Phase2), .Q(register_3_q), .clr(Reset));
  or or_1 (or_1_out, Phase2s, Phase2n);
  Register #(.trigger("high"), .width(5)) A_Address (
    .D(multiplexer_1_out), .en(or_1_out), .clk(or_1_out), .Q({A_Address_q_2[0], A_Address_q}), .clr(Reset));
  Multiplexer #(.width(5)) multiplexer_1 (
    .in0(register_1_q), .in1(register_3_q), .out(multiplexer_1_out), .sel(Phase2s));
  Register #(.trigger("high"), .width(5)) B_Address (
    .D(register_2_q), .en(or_1_out), .clk(or_1_out), .Q({A_Address_q_2[1], B_Address_q}), .clr(Reset));
  Register #(.trigger("high"), .width(5)) C_Address (
    .D(register_3_q), .en(or_1_out), .clk(or_1_out), .Q({A_Address_q_2[2], C_Address_q}), .clr(Reset));
  CWP_And_Address_Decoder cwp_and_address_decoder_1 (
    .A_Address({A_Address_q_2[0], A_Address_q}), .B_Address({A_Address_q_2[1], B_Address_q}),
    .C_Address({A_Address_q_2[2], C_Address_q}), .Enable_Write(Phase3n), .Enable_Read(Phase1n),
    .Context_Window_Pointer(Window_Number),
    .Decoded_Enables({cwp_and_address_decoder_1_decoded_enables_8, cwp_and_address_decoder_1_decoded_enables_7, cwp_and_address_decoder_1_decoded_enables_6, cwp_and_address_decoder_1_decoded_enables_5, cwp_and_address_decoder_1_decoded_enables_4, cwp_and_address_decoder_1_decoded_enables_3, cwp_and_address_decoder_1_decoded_enables_2, cwp_and_address_decoder_1_decoded_enables}));
  assign and_1_out = ~A_Address_q_2 & {Phase3n, {2{Phase1n}}};  // AND_Gate and_1, 3 bits wide
  Register_Window register_window_1 (
    .Address_A(A_Address_q), .Address_B(B_Address_q),
    .Read_Enable_A(cwp_and_address_decoder_1_decoded_enables_8[0]),
    .Read_Enable_B(cwp_and_address_decoder_1_decoded_enables_8[1]), .Reset(Reset), .Data_In(C_Bus_In),
    .Address_C(C_Address_q), .Write_Enable(cwp_and_address_decoder_1_decoded_enables_8[2]),
    .A_Data_Out(A_Bus_Out), .B_Data_Out(B_Bus_Out));
  Register_Window register_window_2 (
    .Address_A(A_Address_q), .Address_B(B_Address_q),
    .Read_Enable_A(cwp_and_address_decoder_1_decoded_enables_6[0]),
    .Read_Enable_B(cwp_and_address_decoder_1_decoded_enables_6[1]), .Reset(Reset), .Data_In(C_Bus_In),
    .Address_C(C_Address_q), .Write_Enable(cwp_and_address_decoder_1_decoded_enables_6[2]),
    .A_Data_Out(A_Bus_Out), .B_Data_Out(B_Bus_Out));
  Register_Window register_window_3 (
    .Address_A(A_Address_q), .Address_B(B_Address_q),
    .Read_Enable_A(cwp_and_address_decoder_1_decoded_enables_4[0]),
    .Read_Enable_B(cwp_and_address_decoder_1_decoded_enables_4[1]), .Reset(Reset), .Data_In(C_Bus_In),
    .Address_C(C_Address_q), .Write_Enable(cwp_and_address_decoder_1_decoded_enables_4[2]),
    .A_Data_Out(A_Bus_Out), .B_Data_Out(B_Bus_Out));
  Register_Window register_window_4 (
    .Address_A(A_Address_q), .Address_B(B_Address_q),
    .Read_Enable_A(cwp_and_address_decoder_1_decoded_enables_2[0]),
    .Read_Enable_B(cwp_and_address_decoder_1_decoded_enables_2[1]), .Reset(Reset), .Data_In(C_Bus_In),
    .Address_C(C_Address_q), .Write_Enable(cwp_and_address_decoder_1_decoded_enables_2[2]),
    .A_Data_Out(A_Bus_Out), .B_Data_Out(B_Bus_Out));
  Global_Registers global_registers_1 (
    .Address_A(A_Address_q), .Address_B(B_Address_q), .Read_Enable_A(and_1_out[0]),
    .Read_Enable_B(and_1_out[1]), .Reset(Reset), .Data_In(C_Bus_In), .Address_C(C_Address_q),
    .Write_Enable(and_1_out[2]), .A_Data_Out(A_Bus_Out), .B_Data_Out(B_Bus_Out));
  Register_Window register_window_5 (
    .Address_A(A_Address_q), .Address_B(B_Address_q),
    .Read_Enable_A(cwp_and_address_decoder_1_decoded_enables_7[0]),
    .Read_Enable_B(cwp_and_address_decoder_1_decoded_enables_7[1]), .Reset(Reset), .Data_In(C_Bus_In),
    .Address_C(C_Address_q), .Write_Enable(cwp_and_address_decoder_1_decoded_enables_7[2]),
    .A_Data_Out(A_Bus_Out), .B_Data_Out(B_Bus_Out));
  Register_Window register_window_6 (
    .Address_A(A_Address_q), .Address_B(B_Address_q),
    .Read_Enable_A(cwp_and_address_decoder_1_decoded_enables_5[0]),
    .Read_Enable_B(cwp_and_address_decoder_1_decoded_enables_5[1]), .Reset(Reset), .Data_In(C_Bus_In),
    .Address_C(C_Address_q), .Write_Enable(cwp_and_address_decoder_1_decoded_enables_5[2]),
    .A_Data_Out(A_Bus_Out), .B_Data_Out(B_Bus_Out));
  Register_Window register_window_7 (
    .Address_A(A_Address_q), .Address_B(B_Address_q),
    .Read_Enable_A(cwp_and_address_decoder_1_decoded_enables_3[0]),
    .Read_Enable_B(cwp_and_address_decoder_1_decoded_enables_3[1]), .Reset(Reset), .Data_In(C_Bus_In),
    .Address_C(C_Address_q), .Write_Enable(cwp_and_address_decoder_1_decoded_enables_3[2]),
    .A_Data_Out(A_Bus_Out), .B_Data_Out(B_Bus_Out));
  Register_Window register_window_8 (
    .Address_A(A_Address_q), .Address_B(B_Address_q),
    .Read_Enable_A(cwp_and_address_decoder_1_decoded_enables[0]),
    .Read_Enable_B(cwp_and_address_decoder_1_decoded_enables[1]), .Reset(Reset), .Data_In(C_Bus_In),
    .Address_C(C_Address_q), .Write_Enable(cwp_and_address_decoder_1_decoded_enables[2]),
    .A_Data_Out(A_Bus_Out), .B_Data_Out(B_Bus_Out));
endmodule

module Global_Registers (
  input  [3:0] Address_A,
  input  Read_Enable_A,
  input  Reset,
  input  [31:0] Data_In,
  input  [3:0] Address_C,
  input  Write_Enable,
  input  [3:0] Address_B,
  input  Read_Enable_B,
  output [31:0] A_Data_Out,
  output [31:0] B_Data_Out
);

  wire decoder_1_out0, decoder_1_out1, decoder_1_out2, decoder_1_out3, decoder_1_out4, decoder_1_out5,
       decoder_1_out6, decoder_1_out7, decoder_1_out8, decoder_1_out9, decoder_1_out10, decoder_1_out11,
       decoder_1_out12, decoder_1_out13, decoder_1_out14, decoder_1_out15;
  wire [31:0] Reg1_q, Reg2_q, Reg3_q, Reg4_q, Reg5_q, Reg6_q, Reg7_q, Reg8_q, Reg9_q, undriven, undriven_2,
       undriven_3, undriven_4, undriven_5, undriven_6;

  Decoder #(.select(4)) decoder_1 (
    .out0(decoder_1_out0), .out1(decoder_1_out1), .out2(decoder_1_out2), .out3(decoder_1_out3),
    .out4(decoder_1_out4), .out5(decoder_1_out5), .out6(decoder_1_out6), .out7(decoder_1_out7),
    .out8(decoder_1_out8), .out9(decoder_1_out9), .out10(decoder_1_out10), .out11(decoder_1_out11),
    .out12(decoder_1_out12), .out13(decoder_1_out13), .out14(decoder_1_out14), .out15(decoder_1_out15),
    .sel(Address_C), .en(Write_Enable));
  // NoConnect on decoder_1_out15
  // NoConnect on decoder_1_out14
  // NoConnect on decoder_1_out13
  // NoConnect on decoder_1_out12
  // NoConnect on decoder_1_out11
  // NoConnect on decoder_1_out10
  // NoConnect on decoder_1_out0
  Register #(.trigger("high"), .width(32)) Reg2 (
    .D(Data_In), .en(decoder_1_out2), .clk(decoder_1_out2), .Q(Reg2_q), .clr(Reset));
  Register #(.trigger("high"), .width(32)) Reg4 (
    .D(Data_In), .en(decoder_1_out4), .clk(decoder_1_out4), .Q(Reg4_q), .clr(Reset));
  Register #(.trigger("high"), .width(32)) Reg6 (
    .D(Data_In), .en(decoder_1_out6), .clk(decoder_1_out6), .Q(Reg6_q), .clr(Reset));
  Register #(.trigger("high"), .width(32)) Reg8 (
    .D(Data_In), .en(decoder_1_out8), .clk(decoder_1_out8), .Q(Reg8_q), .clr(Reset));
  Register #(.trigger("high"), .width(32)) Reg1 (
    .D(Data_In), .en(decoder_1_out1), .clk(decoder_1_out1), .Q(Reg1_q), .clr(Reset));
  Register #(.trigger("high"), .width(32)) Reg3 (
    .D(Data_In), .en(decoder_1_out3), .clk(decoder_1_out3), .Q(Reg3_q), .clr(Reset));
  Register #(.trigger("high"), .width(32)) Reg5 (
    .D(Data_In), .en(decoder_1_out5), .clk(decoder_1_out5), .Q(Reg5_q), .clr(Reset));
  Register #(.trigger("high"), .width(32)) Reg7 (
    .D(Data_In), .en(decoder_1_out7), .clk(decoder_1_out7), .Q(Reg7_q), .clr(Reset));
  Register #(.trigger("high"), .width(32)) Reg9 (
    .D(Data_In), .en(decoder_1_out9), .clk(decoder_1_out9), .Q(Reg9_q), .clr(Reset));
  // NoConnect on undriven
  // NoConnect on undriven_2
  // NoConnect on undriven_3
  // NoConnect on undriven_4
  // NoConnect on undriven_5
  // NoConnect on undriven_6
  Multiplexer #(.disabled("Z"), .enable("true"), .select(4), .width(32)) multiplexer_1 (
    .in0({32{1'b0}}), .in1(Reg1_q), .in2(Reg2_q), .in3(Reg3_q), .in4(Reg4_q), .in5(Reg5_q), .in6(Reg6_q),
    .in7(Reg7_q), .in8(Reg8_q), .in9(Reg9_q), .in10(undriven), .in11(undriven_2), .in12(undriven_3),
    .in13(undriven_4), .in14(undriven_5), .in15(undriven_6), .out(A_Data_Out), .sel(Address_A),
    .en(Read_Enable_A));
  Multiplexer #(.disabled("Z"), .enable("true"), .select(4), .width(32)) multiplexer_2 (
    .in0({32{1'b0}}), .in1(Reg1_q), .in2(Reg2_q), .in3(Reg3_q), .in4(Reg4_q), .in5(Reg5_q), .in6(Reg6_q),
    .in7(Reg7_q), .in8(Reg8_q), .in9(Reg9_q), .in10(undriven), .in11(undriven_2), .in12(undriven_3),
    .in13(undriven_4), .in14(undriven_5), .in15(undriven_6), .out(B_Data_Out), .sel(Address_B),
    .en(Read_Enable_B));

  // Notes on the sheet:
  //   Reg0
endmodule

module CWP_And_Address_Decoder (
  input  [4:0] A_Address,
  input  [4:0] B_Address,
  input  [4:0] C_Address,
  input  Enable_Write,
  input  Enable_Read,
  input  [2:0] Context_Window_Pointer,
  output [23:0] Decoded_Enables
);

  wire and_1_out, and_2_out, and_3_out, and_4_out, and_5_out, and_6_out, and_7_out, and_8_out, and_9_out,
       or_1_out, or_2_out, or_3_out;
  wire [2:0] and_12_out, and_15_out, demultiplexer_1_out0, demultiplexer_1_out1, demultiplexer_1_out2,
       demultiplexer_1_out3, demultiplexer_1_out4, demultiplexer_1_out5, demultiplexer_1_out6,
       demultiplexer_1_out7, demultiplexer_2_out0, demultiplexer_2_out1, demultiplexer_2_out2,
       demultiplexer_2_out3, demultiplexer_2_out4, demultiplexer_2_out5, demultiplexer_2_out6,
       demultiplexer_2_out7, subtractor_1_out;

  or or_1 (or_1_out, A_Address[1], A_Address[2]);
  and and_1 (and_1_out, A_Address[3], ~A_Address[4]);  // AND_Gate
  or or_2 (or_2_out, B_Address[1], B_Address[2]);
  and and_2 (and_2_out, B_Address[3], ~B_Address[4]);  // AND_Gate
  or or_3 (or_3_out, C_Address[1], C_Address[2]);
  and and_3 (and_3_out, C_Address[3], ~C_Address[4]);  // AND_Gate
  and and_4 (and_4_out, or_1_out, and_1_out);
  and and_5 (and_5_out, or_2_out, and_2_out);
  and and_6 (and_6_out, or_3_out, and_3_out);
  Subtractor #(.width(3)) subtractor_1 (
    .a(Context_Window_Pointer), .b(3'b001), .out(subtractor_1_out));  // open: bin, bout
  and and_7 (and_7_out, A_Address[4], ~and_4_out);  // AND_Gate
  and and_8 (and_8_out, B_Address[4], ~and_5_out);  // AND_Gate
  and and_9 (and_9_out, C_Address[4], ~and_6_out);  // AND_Gate
  and and_10 (and_12_out[2], and_9_out, Enable_Read);
  and and_11 (and_12_out[1], and_8_out, Enable_Write);
  and and_12 (and_12_out[0], and_7_out, Enable_Write);
  Demultiplexer #(.select(3), .width(3)) demultiplexer_1 (
    .out0(demultiplexer_1_out0), .out1(demultiplexer_1_out1), .out2(demultiplexer_1_out2),
    .out3(demultiplexer_1_out3), .out4(demultiplexer_1_out4), .out5(demultiplexer_1_out5),
    .out6(demultiplexer_1_out6), .out7(demultiplexer_1_out7), .in(and_12_out), .sel(Context_Window_Pointer));
  and and_13 (and_15_out[2], and_6_out, Enable_Read);
  and and_14 (and_15_out[1], and_5_out, Enable_Write);
  and and_15 (and_15_out[0], and_4_out, Enable_Write);
  Demultiplexer #(.select(3), .width(3)) demultiplexer_2 (
    .out0(demultiplexer_2_out0), .out1(demultiplexer_2_out1), .out2(demultiplexer_2_out2),
    .out3(demultiplexer_2_out3), .out4(demultiplexer_2_out4), .out5(demultiplexer_2_out5),
    .out6(demultiplexer_2_out6), .out7(demultiplexer_2_out7), .in(and_15_out), .sel(subtractor_1_out));
  assign Decoded_Enables = {demultiplexer_1_out7, demultiplexer_1_out6, demultiplexer_1_out5, demultiplexer_1_out4, demultiplexer_1_out3, demultiplexer_1_out2, demultiplexer_1_out1, demultiplexer_1_out0} | {demultiplexer_2_out7, demultiplexer_2_out6, demultiplexer_2_out5, demultiplexer_2_out4, demultiplexer_2_out3, demultiplexer_2_out2, demultiplexer_2_out1, demultiplexer_2_out0};  // OR_Gate or_4, 24 bits wide
  // Probe on {demultiplexer_1_out7, demultiplexer_1_out6, demultiplexer_1_out5, demultiplexer_1_out4, demultiplexer_1_out3, demultiplexer_1_out2, demultiplexer_1_out1, demultiplexer_1_out0}
  // Probe on {demultiplexer_2_out7, demultiplexer_2_out6, demultiplexer_2_out5, demultiplexer_2_out4, demultiplexer_2_out3, demultiplexer_2_out2, demultiplexer_2_out1, demultiplexer_2_out0}
  // Probe on Decoded_Enables

  // Notes on the sheet:
  //   Is lower window address?
endmodule

module Operation_Controller (
  input  [31:0] P_Bus_In,
  input  Phase1,
  input  [3:0] CNZV_In,
  input  Phase2n,
  output Jump,
  output No_Destination,
  output Load,
  output Store,
  output Signed_Load,
  output [1:0] Data_Size,
  output [1:0] Shift_Operation,
  output Shift,
  output Load_Immediate_High,
  output ALU_Enabled,
  output [3:0] ALU_Operation,
  output Get_Last_Program_Counter,
  output Jump_Instruction,
  output Call,
  output Return_Instruction,
  output Relative,
  output Interrupt
);

  wire condition_decoder_1_always, condition_decoder_1_carry_clear, condition_decoder_1_carry_set,
       condition_decoder_1_equal, condition_decoder_1_greater, condition_decoder_1_greater_or_equal,
       condition_decoder_1_higher, condition_decoder_1_is_negative, condition_decoder_1_is_positive,
       condition_decoder_1_less, condition_decoder_1_less_or_equal, condition_decoder_1_lower_or_same,
       condition_decoder_1_never, condition_decoder_1_not_equal, condition_decoder_1_overflow_clear,
       condition_decoder_1_overflow_set, multiplexer_1_out;
  wire [3:0] CNZV_q, Condition_Code_Select_q;
  wire [6:0] Opcode_Input_q;

  Register #(.trigger("high"), .width(4)) Condition_Code_Select (
    .D(P_Bus_In[11:8]), .en(Phase1), .clk(Phase1), .Q(Condition_Code_Select_q));  // open: clr
  Register #(.trigger("high"), .width(4)) CNZV (.D(CNZV_In), .en(Phase1), .clk(Phase1), .Q(CNZV_q));  // open: clr
  Register #(.trigger("high"), .width(7)) Opcode_Input (
    .D(P_Bus_In[6:0]), .en(Phase2n), .clk(Phase2n), .Q(Opcode_Input_q));  // open: clr
  Condition_Decoder condition_decoder_1 (
    .Carry_In(CNZV_q[0]), .Negative(CNZV_q[1]), .Zero(CNZV_q[2]), .Overflow(CNZV_q[3]),
    .Always(condition_decoder_1_always), .Never(condition_decoder_1_never),
    .Not_Equal(condition_decoder_1_not_equal), .Equal(condition_decoder_1_equal),
    .Greater(condition_decoder_1_greater), .Greater_Or_Equal(condition_decoder_1_greater_or_equal),
    .Less(condition_decoder_1_less), .Less_Or_Equal(condition_decoder_1_less_or_equal),
    .Is_Positive(condition_decoder_1_is_positive), .Is_Negative(condition_decoder_1_is_negative),
    .Higher(condition_decoder_1_higher), .Lower_Or_Same(condition_decoder_1_lower_or_same),
    .Overflow_Clear(condition_decoder_1_overflow_clear), .Overflow_Set(condition_decoder_1_overflow_set),
    .Carry_Clear(condition_decoder_1_carry_clear), .Carry_Set(condition_decoder_1_carry_set));
  Operation_Decoder operation_decoder_1 (
    .Opcode(Opcode_Input_q), .No_Destination(No_Destination), .Load(Load), .Store(Store),
    .Signed_Load(Signed_Load), .Data_Size(Data_Size), .Shift_Operation(Shift_Operation), .Shift(Shift),
    .Load_Immediate_High(Load_Immediate_High), .ALU_Enable(ALU_Enabled), .ALU_Operation(ALU_Operation),
    .Get_Last_Program_Counter(Get_Last_Program_Counter), .Jump_Instruction(Jump_Instruction), .Call(Call),
    .Return_Instruction(Return_Instruction), .Relative(Relative), .Interrupt(Interrupt));
  Multiplexer #(.select(4)) multiplexer_1 (
    .in0(condition_decoder_1_always), .in1(condition_decoder_1_never), .in2(condition_decoder_1_not_equal),
    .in3(condition_decoder_1_equal), .in4(condition_decoder_1_greater),
    .in5(condition_decoder_1_greater_or_equal), .in6(condition_decoder_1_less),
    .in7(condition_decoder_1_less_or_equal), .in8(condition_decoder_1_is_positive),
    .in9(condition_decoder_1_is_negative), .in10(condition_decoder_1_higher),
    .in11(condition_decoder_1_lower_or_same), .in12(condition_decoder_1_overflow_clear),
    .in13(condition_decoder_1_overflow_set), .in14(condition_decoder_1_carry_clear),
    .in15(condition_decoder_1_carry_set), .out(multiplexer_1_out), .sel(Condition_Code_Select_q));
  and and_1 (Jump, multiplexer_1_out, Jump_Instruction);
endmodule

module Window_Number_Controller (
  input  Call_Return,
  input  [31:0] LBus_In,
  input  Phi1n,
  input  Phi2n,
  output [31:0] LBus_Out,
  output Window_Overflow,
  output [2:0] Window_Number
);

  wire adder_1_cout, subtractor_1_bout, undriven;
  wire [2:0] adder_1_out, multiplexer_1_out, multiplexer_2_out, register_1_q, subtractor_1_out;

  Multiplexer #(.width(3)) multiplexer_1 (.in0(LBus_In[9:7]), .in1(register_1_q), .out(multiplexer_1_out), .sel(Phi2n));
  Register #(.trigger("high"), .width(3)) Saved_Window_Pointer (
    .D(LBus_In[6:4]), .en(undriven), .clk(undriven), .Q(LBus_Out[6:4]));  // open: clr
  Register #(.trigger("high"), .width(3)) Current_Window_Pointer (
    .D(multiplexer_1_out), .en(Phi2n), .clk(Phi2n), .Q(LBus_Out[9:7]));  // open: clr
  Adder #(.width(3)) adder_1 (.a(LBus_Out[9:7]), .b(3'b001), .out(adder_1_out), .cout(adder_1_cout));  // open: cin
  Subtractor #(.width(3)) subtractor_1 (
    .a(LBus_Out[9:7]), .b(3'b001), .out(subtractor_1_out), .bout(subtractor_1_bout));  // open: bin
  Multiplexer #(.width(3)) multiplexer_2 (
    .in0(adder_1_out), .in1(subtractor_1_out), .out(multiplexer_2_out), .sel(Call_Return));
  Multiplexer multiplexer_3 (.in0(adder_1_cout), .in1(subtractor_1_bout), .out(Window_Overflow), .sel(Call_Return));
  Register #(.trigger("high"), .width(3)) register_1 (
    .D(multiplexer_2_out), .en(Phi1n), .clk(Phi1n), .Q(register_1_q));  // open: clr

  assign Window_Number = LBus_Out[9:7];
endmodule

module Operation_Decoder (
  input  [6:0] Opcode,
  output No_Destination,
  output Load,
  output Store,
  output Signed_Load,
  output [1:0] Data_Size,
  output [1:0] Shift_Operation,
  output Shift,
  output Load_Immediate_High,
  output ALU_Enable,
  output [3:0] ALU_Operation,
  output Get_Last_Program_Counter,
  output Jump_Instruction,
  output Call,
  output Return_Instruction,
  output Relative,
  output Interrupt
);

  wire not_1_out, not_2_out, not_3_out, not_4_out, not_5_out, not_6_out, or_1_out, or_2_out, or_3_out,
       or_4_out, or_5_out, or_6_out, or_7_out, or_8_out, or_9_out, or_10_out, or_11_out, or_12_out,
       or_13_out, or_14_out, or_15_out, or_16_out, or_17_out, or_18_out, or_19_out, or_20_out, or_21_out,
       or_22_out, or_23_out, or_24_out, or_25_out, or_26_out;

  not not_1 (not_1_out, Opcode[6]);
  not not_2 (not_2_out, Opcode[5]);
  not not_3 (not_3_out, Opcode[4]);
  not not_4 (not_4_out, Opcode[3]);
  not not_5 (not_5_out, Opcode[2]);
  not not_6 (not_6_out, Opcode[1]);
  and and_1 (No_Destination, Opcode[5], Opcode[4], not_1_out);
  or or_1 (or_1_out, Opcode[3], Opcode[2]);
  and and_2 (Store, Opcode[5], Opcode[4], not_1_out);
  and and_3 (Signed_Load, Opcode[1], not_1_out);
  or or_2 (or_2_out, Opcode[4], not_5_out);
  or or_3 (or_3_out, Opcode[4], Opcode[3]);
  or or_4 (or_4_out, Opcode[3], not_5_out);
  and and_4 (Shift_Operation[1], Opcode[3], Opcode[2]);
  or or_5 (or_5_out, Opcode[3], not_6_out);
  or or_6 (or_6_out, Opcode[2], not_6_out);
  and and_5 (Load_Immediate_High, Opcode[6], Opcode[5], Opcode[4]);
  or or_7 (or_7_out, Opcode[6], not_3_out);
  or or_8 (or_8_out, Opcode[6], not_2_out);
  or or_9 (or_9_out, not_2_out, Opcode[4], not_4_out);
  and and_6 (ALU_Operation[3], Opcode[4], Opcode[2], not_4_out, not_2_out);
  or or_10 (or_10_out, not_1_out, Opcode[5], Opcode[4]);
  or or_11 (or_11_out, not_1_out, not_2_out, not_3_out);
  or or_12 (or_12_out, not_1_out, Opcode[5], Opcode[3], Opcode[2]);
  or or_13 (or_13_out, not_1_out, not_3_out, Opcode[3]);
  or or_14 (or_14_out, not_1_out, not_2_out, not_3_out);
  or or_15 (or_15_out, Opcode[4], Opcode[3], not_5_out);
  or or_16 (or_16_out, not_3_out, not_4_out, Opcode[2]);
  or or_17 (or_17_out, not_3_out, Opcode[3], Opcode[1]);
  and and_7 (Get_Last_Program_Counter, Opcode[6], Opcode[5], Opcode[3], not_3_out);
  and and_8 (Jump_Instruction, Opcode[3], Opcode[1], not_3_out, not_2_out, not_1_out);
  or or_18 (or_18_out, not_4_out, not_6_out);
  and and_9 (Return_Instruction, Opcode[6], Opcode[5], not_4_out, not_3_out);
  or or_19 (or_19_out, Opcode[5], Opcode[3]);
  or or_20 (or_20_out, Opcode[5], Opcode[2]);
  or or_21 (or_21_out, Opcode[5], not_3_out);
  or or_22 (or_22_out, Opcode[4], Opcode[3], Opcode[2]);
  or or_23 (or_23_out, not_2_out, Opcode[0]);
  or or_24 (or_24_out, Opcode[6], not_2_out);
  or or_25 (or_25_out, not_1_out, Opcode[5]);
  or or_26 (or_26_out, not_1_out, Opcode[2]);
  and and_10 (Load, Opcode[5], or_1_out, not_3_out, not_1_out);
  and and_11 (Data_Size[1], Opcode[5], Opcode[3], or_2_out, not_1_out);
  and and_12 (Data_Size[0], Opcode[5], or_3_out, or_4_out, not_1_out);
  and and_13 (Shift, Opcode[4], or_5_out, or_6_out, not_2_out, not_1_out);
  and and_14 (ALU_Enable, or_7_out, or_8_out, or_9_out);
  and and_15 (ALU_Operation[2], or_10_out, or_11_out);
  and and_16 (ALU_Operation[1], or_12_out, or_13_out, or_14_out);
  and and_17 (ALU_Operation[0], Opcode[6], or_15_out, or_16_out, not_2_out, or_17_out);
  and and_18 (Call, or_18_out, not_3_out, not_2_out, not_1_out);
  and and_19 (Relative, or_19_out, or_20_out, or_21_out, or_22_out, or_23_out, not_1_out);
  and and_20 (Interrupt, not_4_out, not_3_out, or_24_out, or_25_out, or_26_out);

  assign Shift_Operation[0] = Opcode[3];
endmodule

module Condition_Decoder (
  input  Carry_In,
  input  Negative,
  input  Zero,
  input  Overflow,
  output Always,
  output Never,
  output Not_Equal,
  output Equal,
  output Greater,
  output Greater_Or_Equal,
  output Less,
  output Less_Or_Equal,
  output Is_Positive,
  output Is_Negative,
  output Higher,
  output Lower_Or_Same,
  output Overflow_Clear,
  output Overflow_Set,
  output Carry_Clear,
  output Carry_Set
);

  not not_1 (Carry_Clear, Carry_In);
  not not_2 (Is_Positive, Negative);
  not not_3 (Not_Equal, Zero);
  not not_4 (Overflow_Clear, Overflow);
  or or_1 (Greater_Or_Equal, Overflow, Negative);
  and and_1 (Greater, Not_Equal, Greater_Or_Equal);
  and and_2 (Higher, Carry_In, Not_Equal);
  not not_5 (Less, Greater_Or_Equal);
  not not_6 (Less_Or_Equal, Greater);
  not not_7 (Lower_Or_Same, Higher);

  assign Always = 1'b1;
  assign Carry_Set = Carry_In;
  assign Equal = Zero;
  assign Is_Negative = Negative;
  assign Never = 1'b0;
  assign Overflow_Set = Overflow;
endmodule
